// Logisim project full_adder.circ as structural Verilog: 1 circuit, main circuit main
module main (
  input  C,
  input  B,
  input  A,
  output Carry,
  output Sum
);

  wire and_1_out, and_2_out, and_3_out, or_1_out, xor_1_out;

  and and_1 (and_1_out, A, B);
  and and_2 (and_2_out, A, C);
  and and_3 (and_3_out, B, C);
  or or_1 (or_1_out, and_1_out, and_2_out);
  xor xor_1 (xor_1_out, A, B);
  or or_2 (Carry, or_1_out, and_3_out);
  xor xor_2 (Sum, xor_1_out, C);
endmodule
