// Logisim project multiplier_2bit.circ as structural Verilog: 1 circuit, main circuit main
module main (
  input  B0,
  input  B1,
  input  A0,
  input  A1,
  output Q3,
  output Q2,
  output Q1,
  output Q0
);

  wire and_1_out, and_2_out, and_3_out, and_5_out;

  and and_1 (and_1_out, A1, B1);
  and and_2 (and_2_out, B0, A1);
  and and_3 (and_3_out, B1, A0);
  and and_4 (Q0, B0, A0);
  and and_5 (and_5_out, and_2_out, and_3_out);
  xor xor_1 (Q1, and_2_out, and_3_out);
  and and_6 (Q3, and_1_out, and_5_out);
  xor xor_2 (Q2, and_1_out, and_5_out);
endmodule
