// Logisim project mux_4to1.circ as structural Verilog: 1 circuit, main circuit main
module main (
  input  S1,
  input  S0,
  input  D,
  input  C,
  input  B,
  input  A,
  output Z
);

  wire and_1_out, and_2_out, and_3_out, and_4_out, not_1_out, not_2_out;

  not not_1 (not_1_out, S1);
  not not_2 (not_2_out, S0);
  and and_1 (and_1_out, S1, S0, D);
  and and_2 (and_2_out, S1, not_2_out, C);
  and and_3 (and_3_out, not_1_out, S0, B);
  and and_4 (and_4_out, not_1_out, not_2_out, A);
  or or_1 (Z, and_1_out, and_2_out, and_3_out, and_4_out);
endmodule
